// Logisim project nand_nor.circ as structural Verilog: 1 circuit, main circuit main
module main (
  input  in_1,
  input  in_2,
  input  in_3,
  input  in_4,
  input  in_5,
  input  in_6,
  input  in_7,
  input  in_8
);

  wire clock_1_out, clock_2_out, clock_3_out, clock_4_out, nand_1_out, nand_2_out, nand_3_out, nand_4_out,
       nor_1_out, nor_2_out, nor_3_out, nor_4_out;

  Clock clock_1 (.out(clock_1_out));
  Clock clock_2 (.out(clock_2_out));
  nand nand_1 (nand_1_out, in_1, clock_1_out);
  nand nand_2 (nand_2_out, in_5, clock_2_out);
  nor nor_1 (nor_1_out, nand_1_out, in_3);
  nor nor_2 (nor_2_out, nand_2_out, in_7);
  LED led_1 (.in(nor_1_out));
  LED led_2 (.in(nor_2_out));
  Clock clock_3 (.out(clock_3_out));
  Clock clock_4 (.out(clock_4_out));
  nand nand_3 (nand_3_out, in_2, clock_3_out);
  nand nand_4 (nand_4_out, in_6, clock_4_out);
  nor nor_3 (nor_3_out, nand_3_out, in_4);
  nor nor_4 (nor_4_out, nand_4_out, in_8);
  LED led_3 (.in(nor_3_out));
  LED led_4 (.in(nor_4_out));
endmodule
